# Fritzing sketch PiSketch (saved by Fritzing 0.9.3b)
breadboards: 1

parts:
  Raspberry_Pi_1 = Raspberry Pi 3 [part_number=RPI-3-V1.2]
  R1 = Photocell (LDR) [package=THT]

nets:
  N1: Raspberry_Pi_1.3v3, R1.pin_1
  N2: Raspberry_Pi_1.GPIO4, Raspberry_Pi_1.GND, R1.pin_0
